# Fritzing sketch qn8035-rpi3-connection (saved by Fritzing 0.9.3b)

parts:
  Part1 = QN8035 FM radio receiver [part_number=QN8035]
  Raspberry_Pi_1 = Raspberry Pi 3 [part_number=RPI-3-V1.2]

nets:
  N1: Part1.SCL, Raspberry_Pi_1.GPIO3
  N2: Part1.SDA, Raspberry_Pi_1.GPIO2
  VCC: Part1.VCC, Raspberry_Pi_1.3v3
  GND: Part1.GND, Raspberry_Pi_1.GND

notes:
  QN8035 Tuner Board
  Raspberry Pi 3 Model B
  Antenna Wire (30cm - 40cm)
  AF Output

custom parts:
  QN8035 FM radio receiver: QN8035 based Raspberry Pi FM radio receiver.
